# Fritzing sketch pi_rfm69 (saved by Fritzing 0.9.3b)

parts:
  RFM1 = RFM69HCW ISM Transciever
  Raspberry_Pi = Raspberry Pi 2

nets:
  N1: RFM1.2_MISO, Raspberry_Pi.GPIO9
  N2: RFM1.3_MOSI, Raspberry_Pi.GPIO10
  N3: RFM1.4_SCK, Raspberry_Pi.GPIO11
  N4: RFM1.5_NSS_(CS), Raspberry_Pi.GPIO8
  N5: RFM1.10_GND, Raspberry_Pi.GND
  N6: RFM1.13_3.3V, Raspberry_Pi.3v3
  N7: RFM1.14_DIO0, Raspberry_Pi.GPIO25

notes:
  Antenna

custom parts:
  RFM69HCW ISM Transciever: RF Transceiver by Hope RF. Well supported Arduino libraries are available. This ISM band transceiver is available in several frequencies e.g. 433MHz and 915MHz and it is also available in various feature versions.
